# Fritzing sketch rangkaian (saved by Fritzing 0.9.3b)
breadboards: 1

parts:
  Part1 = Arduino Uno (Rev3) - ICSP
  DHT1 = DHT22 Humidity and Temperature Sensor
  Part2 = MQ-3 breakout
  ZS-042_RTC1 = ZS-042 RTC Module
  Part3 = DC-DC Power Module (5v)
  J2 = Power Jack [package=power_jack_smd]
  Part4 = SRF05 Ultrasonic Rangefinder
  J3 = Piezo Speaker

nets:
  N1: Part1.A0, Part2.AO
  N2: Part1.A5/SCL, ZS-042_RTC1.SCL
  N3: Part1.D8, J3.pin2
  N4: Part1.D9_PWM, DHT1.DATA
  N5: Part1.D10_PWM/SS, Part4.Echo
  N6: Part1.D11_PWM/MOSI, Part4.Trig
  GND: Part1.GND, DHT1.GND, Part2.GND, ZS-042_RTC1.GND, Part3.GND*, Part4.GND, J3.pin1
  VCC: Part1.VIN, DHT1.VDD, Part2.VCC, ZS-042_RTC1.VCC, Part3.Vout, Part4.VCC
  N7: Part3.Vin, J2.PWR
  GND_2: Part3.GND, J2.GND

custom parts:
  MQ-3 breakout: Alcohol sensor is capable of detecting alcohol (ethanol) particles on itself and gives the information in digital form back to us to manipulate with it. SKU:101251 • Voltage: 5V DC • Power: max 750mW • Measurement range: 0.04-4mg/L
  DC-DC Power Module (5v): DC-DC Power Module based con AMS1117-5.0 Input: DC 6~12V (input power must higher 1V than output power); Output: 5V (+/-0.05V error), 800mA
